// Logisim project bf.circ as structural Verilog
module ALU (
  input  [7:0] \input ,
  input  [3:0] opcode,
  output [7:0] \output 
);

  wire [7:0] adder_1_out, subtractor_1_out;

  Adder adder_1 (.a(\input ), .b(8'h1), .out(adder_1_out));  // open: cin, cout
  Subtractor subtractor_1 (.a(\input ), .b(8'h1), .out(subtractor_1_out));  // open: bin, bout
  Multiplexer #(.select(4), .width(8), .enable("false")) multiplexer_1 (
    .in1(adder_1_out), .in2(subtractor_1_out), .in3(adder_1_out), .in4(subtractor_1_out), .out(\output ),
    .sel(opcode));  // open: in0, in5, in6, in7, in8, in9, in10, in11, in12, in13, in14, in15
endmodule

module Decoder (
  input  [7:0] instruction,
  output [3:0] out_2
);

  ROM #(.dataWidth(4)) rom_1 (.addr(instruction), .data(out_2));  // open: sel

  // Notes on the sheet:
  //   contents of rom_1 (hex, n*v repeats v):
  //   43*0 3 6 4 5 13*0 2 0 1 28*0 7 8
endmodule
